# Fritzing sketch Protoboard (saved by Fritzing 0.9.3b)
breadboards: 2

parts:
  B1 = Pushbutton [package="[THT]"]
  ESP32s = node32s
  L1 = LED - 5mm [color="Red (633nm)" part_number="LED VERDE" package="5 mm [THT]"]
  R9 = Resistor [tolerance=±5% resistance=220 package=THT]
  4_Channel_Relay1 = 4 Channel Power Relay
  R10 = Resistor [tolerance=±5% resistance=220 package=THT]
  D1 = Diode [part_number=1N4001 package=diode-1n4001]
  Q1 = MOSFET-NCHANNEL [part_number=IRFZ44N package=to220v]
  R5 = Resistor [tolerance=±5% resistance=10k package="0805 [SMD]"]
  R6 = Resistor [tolerance=±5% resistance=10k package="0805 [SMD]"]
  Q3 = MOSFET-NCHANNEL [part_number=IRFZ44N package=to220v]
  R3 = Resistor [tolerance=±5% resistance=10k package="0805 [SMD]"]
  R4 = Resistor [tolerance=±5% resistance=10k package="0805 [SMD]"]
  Q5 = MOSFET-NCHANNEL [part_number=IRFZ44N package=to220v]
  R2 = Resistor [tolerance=±5% resistance=10k package="0805 [SMD]"]
  R1 = Resistor [tolerance=±5% resistance=10k package="0805 [SMD]"]
  J1 = female pin header, 2 pins [form="♀ (female)"]
  J2 = female pin header, 2 pins [form="♀ (female)"]
  R12 = Resistor [tolerance=±5% resistance=220 package=THT]
  R13 = Resistor [tolerance=±5% resistance=220 package=THT]
  Power_supply = 电源转换模块
  IC1 = Voltage Regulator [part_number=MC7805 package=to-220-alt]
  R11 = Resistor [tolerance=±5% resistance=1k package=THT]
  S1 = Round Pushbutton
  S2 = Round Pushbutton
  S3 = Round Pushbutton
  Q4 = NPN-Transistor [package="TO92 [THT]"]
  Q6 = NPN-Transistor [package="TO92 [THT]"]
  Q2 = NPN-Transistor [package="TO92 [THT]"]
  D3 = Rectifier Diode [part_number=1N4001 package="Melf DO-213 AB [SMD]"]
  D4 = Rectifier Diode [part_number=1N4001 package="Melf DO-213 AB [SMD]"]

nets:
  GND: B1.Pin_1, B1.Pin_2, ESP32s.GND, R9.Pin_1, 4_Channel_Relay1.GND, Power_supply.5V-GND-1, IC1.GND, S1.leg0, S2.leg0, S3.leg0
  CONTROL_BUTTON_PIN: B1.Pin_3, B1.Pin_4, ESP32s.IO19
  CEILING PIN: ESP32s.IO32, 4_Channel_Relay1.IN4
  READING 1 PIN: ESP32s.IO33, 4_Channel_Relay1.IN3
  READING 2 PIN: ESP32s.IO25, 4_Channel_Relay1.IN2
  STANDING PIN: ESP32s.IO26, 4_Channel_Relay1.IN1
  PUSHBUTTON_3_PIN: ESP32s.IO27, R13.Pin_1, S1.leg1
  5V: ESP32s.5V, Power_supply.5V-1
  BLUE_ANODE_PIN: ESP32s.IO23, R2.Pin_0
  GREEN_ANODE_PIN: ESP32s.IO22, R5.Pin_0
  N1: ESP32s.RXD, R11.Pin_1
  RED_ANODE_PIN: ESP32s.IO21, R3.Pin_0
  STATUS_LED_PIN: ESP32s.IO18, L1.anode
  PUSHBUTTON_2_PIN: ESP32s.IO17, R12.Pin_1, S3.leg1
  PUSHBUTTON_1_PIN: ESP32s.IO16, R10.Pin_1, S2.leg1
  N2: L1.cathode, R9.Pin_0
  N3: 4_Channel_Relay1.JD-VCC, IC1.OUT
  3.3V: R10.Pin_0, R12.Pin_0, R13.Pin_0, Power_supply.3V3-1, R11.Pin_0
  N4: D1.A, Q1.D, J1.pin2
  12V: D1.C, R6.Pin_1, R4.Pin_1, R1.Pin_1, J1.pin1, IC1.IN, D3.cathode, D4.cathode
  N5: Q1.G, R6.Pin_0, Q2.C
  N6: Q1.S, Q3.S, Q5.S, Power_supply.DC-IN-1, Q4.E, Q6.E, Q2.E
  N7: R5.Pin_1, Q2.B
  N8: Q3.G, R4.Pin_0, Q4.C
  N9: Q3.D, J2.pin1, D3.anode
  N10: R3.Pin_1, Q4.B
  N11: Q5.G, R1.Pin_0, Q6.C
  N12: Q5.D, J2.pin2, D4.anode
  N13: R2.Pin_1, Q6.B
  N14: Power_supply.5V-GND-3, Power_supply.3V3-GND-3, Power_supply.DC-IN-GND-2

custom parts:
  4 Channel Power Relay: A 4 channel power relay. The module operates at 5V.
  电源转换模块: Features: Two wire I2C interface Hour : Minutes : Seconds AM/PM Day Month, Date - Year Leap year compensation Accurate calendar up to year 2100 Battery backup included 1Hz output pin 56 Bytes of Non-volatile memory available to user Dimensions: 0.75x0.75" (20x20mm) Documents: RTC Module Schematic RTC Module Dimensional Drawing DS1307 Datasheet Wiring Example Software: Example 16F88 code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
